// Logisim project cpu.circ as structural Verilog: 42 circuits, main circuit main
module main (
  output [31:0] valM,
  output [1:0] out_2,
  output out_3,
  output [31:0] valE,
  output [31:0] valP,
  output [31:0] valA
);

  wire alu_1_a, alu_1_b, alu_1_c, alu_1_zf, clock_1_out, funit_1_inst_err, funit_1_mem_err, mem_ctrl_1_read,
       mem_ctrl_1_write, or_1_out, timing_helper_1_out, timing_helper_2_out;
  wire [1:0] alufun_1_alua;
  wire [2:0] cnd_1_cnd;
  wire [3:0] alufun_1_alue, dste_1_out_5, dstm_1_out_3, funit_1_icode, funit_1_icode_2, funit_1_ifun,
       funit_1_ra, funit_1_rb, srca_1_out_3, srcb_1_out_3;
  wire [7:0] timing_helper_1_counter, timing_helper_2_counter;
  wire [31:0] alua_1_aluaout, alub_1_alubout, funit_1_valc, mem_addr_1_out_4, mem_data_1_out_4, new_pc_1_out,
       pc_1_out_3, register_file_1_out_13;

  Clock clock_1 (.out(clock_1_out));
  stat stat_1 (.out_4(out_2), .instr_err(funit_1_inst_err), .icode(funit_1_icode), .mem_err(or_1_out));
  PC pc_1 (.Clk(clock_1_out), .out_3(pc_1_out_3), .in_2(new_pc_1_out));
  FUnit funit_1 (
    .Clk(clock_1_out), .icode_2(funit_1_icode_2), .mem_err(funit_1_mem_err), .inst_err(funit_1_inst_err),
    .icode(funit_1_icode), .ifun(funit_1_ifun), .rA(funit_1_ra), .rB(funit_1_rb), .valC(funit_1_valc),
    .new_pc(pc_1_out_3));
  new_pc new_pc_1 (
    .icode(funit_1_icode), .ifun(funit_1_ifun), .Cnd(cnd_1_cnd), .valC(funit_1_valc), .valM(valM),
    .valP(valP), .out(new_pc_1_out));
  or or_1 (or_1_out, out_3, funit_1_mem_err);
  Cnd cnd_1 (
    .Clk(clock_1_out), .icode(funit_1_icode), .Z(alu_1_zf), .A(alu_1_a), .B(alu_1_b), .C(alu_1_c),
    .Current_ALU_Function(alufun_1_alue), .Cnd(cnd_1_cnd));
  ALU alu_1 (
    .ZF(alu_1_zf), .A(alu_1_a), .B(alu_1_b), .C(alu_1_c), .in_4(funit_1_icode), .ValE(valE),
    .valA(alua_1_aluaout), .valB(alub_1_alubout), .Function(alufun_1_alue));
  ALUA alua_1 (.ALUAOUT(alua_1_aluaout), .ValC(funit_1_valc), .ValA(valA), .ALUA_Function(alufun_1_alua));
  // Probe on pc_1_out_3
  mem_ctrl mem_ctrl_1 (.read(mem_ctrl_1_read), .write(mem_ctrl_1_write), .icode(funit_1_icode), .Clk(clock_1_out));
  mem_addr mem_addr_1 (.valE(valE), .valA(valA), .out_4(mem_addr_1_out_4), .icode(funit_1_icode));
  ALUFun alufun_1 (
    .iCode(funit_1_icode), .iFun(funit_1_ifun), .ALUA(alufun_1_alua), .ALUE(alufun_1_alue));  // open: Valid
  ALUB alub_1 (.ALUBOUT(alub_1_alubout), .ValB(register_file_1_out_13));
  data_mem data_mem_1 (
    .read(mem_ctrl_1_read), .write(mem_ctrl_1_write), .Clk(clock_1_out), .valM(valM),
    .addr_in(mem_addr_1_out_4), .data_in(mem_data_1_out_4), .mem_err(out_3));
  mem_data mem_data_1 (.valP(valP), .valA(valA), .out_4(mem_data_1_out_4), .icode(funit_1_icode));
  PCIncr pcincr_1 (.iCode(funit_1_icode_2), .valP(valP), .curPC(pc_1_out_3));
  dstE dste_1 (.icode(funit_1_icode), .rB(funit_1_rb), .out_5(dste_1_out_5), .Cnd(cnd_1_cnd), .ifun(funit_1_ifun));
  register_file register_file_1 (
    .valE(valE), .out_12(valA), .srcA(srca_1_out_3), .destE(dste_1_out_5), .srcB(srcb_1_out_3),
    .destM(dstm_1_out_3), .out_13(register_file_1_out_13), .valM(valM), .in_11(clock_1_out),
    .eDE(timing_helper_1_out), .eDM(timing_helper_1_out), .eSA(1'b1), .eSB(1'b1));
  srcA srca_1 (.icode(funit_1_icode), .rA(funit_1_ra), .out_3(srca_1_out_3));
  dstM dstm_1 (.out_3(dstm_1_out_3), .icode(funit_1_icode), .rA(funit_1_ra));
  srcB srcb_1 (.out_3(srcb_1_out_3), .icode(funit_1_icode), .rB(funit_1_rb));
  timing_helper timing_helper_1 (
    .delay(8'hc), .out(timing_helper_1_out), .in(1'b1), .length(8'h1), .cycle(8'hf), .Clk(clock_1_out),
    .counter(timing_helper_1_counter));
  timing_helper timing_helper_2 (
    .delay(8'hf), .out(timing_helper_2_out), .in(1'b1), .length(8'h1), .cycle(8'hf), .Clk(clock_1_out),
    .counter(timing_helper_2_counter));
  Counter #(.width(16), .max('hffff)) counter_1 (.clk(timing_helper_2_out));  // open: load, D, count, Q, carry, clr
endmodule

module data_mem (
  input  read,
  input  write,
  input  Clk,
  input  [31:0] addr_in,
  input  [31:0] data_in,
  output mem_err,
  output [31:0] valM
);

  wire not_1_out, toggle_1_out, toggle_2_out, xor_1_out;
  wire [3:0] counter_1_q;
  wire [4:0] shifter_1_out;
  wire [4:4] counter_1_carry;
  wire [7:0] adder_1_out_2, bus_buffer_1_o1, ram_1_data, shifter_2_out_2;
  wire [23:0] adder_1_out, shifter_2_out, shifter_3_out;
  wire [31:0] littlee_1_littlee_out;
  wire [31:24] shifter_3_out_2;

  xor xor_1 (xor_1_out, write, read);
  toggle toggle_1 (.in(xor_1_out), .Clk(Clk), .reset(counter_1_carry[4]), .out(toggle_1_out));
  toggle toggle_2 (.in(write), .Clk(Clk), .reset(counter_1_carry[4]), .out(toggle_2_out));
  Counter #(.width(4), .max('h4)) counter_1 (
    .count(toggle_1_out), .Q(counter_1_q), .carry(counter_1_carry[4]), .clk(Clk), .clr(counter_1_carry[4]));  // open: load, D
  not not_1 (not_1_out, toggle_2_out);
  Comparator #(.mode("unsigned")) comparator_1 (.a({8{1'b0}}), .b(adder_1_out_2), .gt(mem_err));  // open: eq, lt
  Adder #(.width(32)) adder_1 (
    .a({{28{1'b0}}, counter_1_q}), .b(addr_in), .out({adder_1_out_2, adder_1_out}));  // open: cin, cout
  Shifter #(.width(5)) shifter_1 (.in({counter_1_carry[4], counter_1_q}), .\dist (3'b011), .out(shifter_1_out));
  RAM #(.addrWidth(24)) ram_1 (
    .addr(adder_1_out), .data(ram_1_data), .sel(toggle_1_out), .clk(Clk), .ld(not_1_out));  // open: clr
  littleE littlee_1 (.bigE_in(data_in), .littleE_out(littlee_1_littlee_out));
  bus_buffer bus_buffer_1 (
    .o0(ram_1_data), .i1(ram_1_data), .in_3(not_1_out), .i0(shifter_2_out_2), .o1(bus_buffer_1_o1));
  Shifter #(.width(32)) shifter_2 (
    .in(littlee_1_littlee_out), .\dist (shifter_1_out), .out({shifter_2_out_2, shifter_2_out}));
  Shifter #(.width(32), .shift("lr")) shifter_3 (.in(valM), .\dist (5'b01000), .out({shifter_3_out_2, shifter_3_out}));
  Register #(.width(32)) register_1 (
    .D({bus_buffer_1_o1, shifter_3_out}), .en(toggle_1_out), .Q(valM), .clk(Clk));  // open: clr

  // Notes on the sheet:
  //   counter
  //   counter * 8
  //   32->24 bit addr
endmodule

// m_ctrl
module mem_ctrl (
  input  Clk,
  input  [3:0] icode,
  output read,
  output write
);

  wire _0x40_out, _0x50_out, _0x80_out, _0x90_out, _0xa0_out, _0xb0_out, or_1_out, or_2_out,
       timing_helper_1_out;

  and _0x50 (_0x50_out, ~icode[3], icode[2], ~icode[1], icode[0]);  // AND_Gate
  or or_1 (or_1_out, _0x50_out, _0x90_out, _0xb0_out);
  and _0x90 (_0x90_out, icode[3], ~icode[2], ~icode[1], icode[0]);  // AND_Gate
  and and_1 (read, or_1_out, timing_helper_1_out);
  and _0xb0 (_0xb0_out, icode[3], ~icode[2], icode[1], icode[0]);  // AND_Gate
  timing_helper timing_helper_1 (
    .delay(8'h7), .out(timing_helper_1_out), .in(1'b1), .length(8'h1), .cycle(8'hf), .Clk(Clk));  // open: counter
  and _0x40 (_0x40_out, ~icode[3], icode[2], ~icode[1], ~icode[0]);  // AND_Gate
  and and_2 (write, timing_helper_1_out, or_2_out);
  or or_2 (or_2_out, _0x40_out, _0x80_out, _0xa0_out);
  and _0x80 (_0x80_out, icode[3], ~icode[2], ~icode[1], ~icode[0]);  // AND_Gate
  and _0xa0 (_0xa0_out, icode[3], ~icode[2], icode[1], ~icode[0]);  // AND_Gate

  // Notes on the sheet:
  //   decide read/write/nothing based on icode
endmodule

// m_addr
module mem_addr (
  input  [3:0] icode,
  input  [31:0] valE,
  input  [31:0] valA,
  output [31:0] out_4
);

  wire _0x40_out, _0x50_out, _0x80_out, _0x90_out, _0xa0_out, _0xb0_out, a_out, e_out, xor_1_out;

  or e (e_out, _0x40_out, _0x50_out, _0xa0_out, _0x80_out);
  and _0x50 (_0x50_out, ~icode[3], icode[2], ~icode[1], icode[0]);  // AND_Gate
  and _0x40 (_0x40_out, ~icode[3], icode[2], ~icode[1], ~icode[0]);  // AND_Gate
  and _0xa0 (_0xa0_out, icode[3], ~icode[2], icode[1], ~icode[0]);  // AND_Gate
  or a (a_out, _0x90_out, _0xb0_out);
  and _0x90 (_0x90_out, icode[3], ~icode[2], ~icode[1], icode[0]);  // AND_Gate
  and _0x80 (_0x80_out, icode[3], ~icode[2], ~icode[1], ~icode[0]);  // AND_Gate
  and _0xb0 (_0xb0_out, icode[3], ~icode[2], icode[1], icode[0]);  // AND_Gate
  xor xor_1 (xor_1_out, e_out, a_out);
  Multiplexer #(.width(32), .disabled(0)) multiplexer_1 (
    .in0(valE), .in1(valA), .out(out_4), .sel(a_out), .en(xor_1_out));
endmodule

// m_data
module mem_data (
  input  [3:0] icode,
  input  [31:0] valP,
  input  [31:0] valA,
  output [31:0] out_4
);

  wire _0x40_out, _0x80_out, _0xa0_out, a_out, xor_1_out;

  and _0x80 (_0x80_out, icode[3], ~icode[2], ~icode[1], ~icode[0]);  // AND_Gate
  or a (a_out, _0x40_out, _0xa0_out);
  and _0x40 (_0x40_out, ~icode[3], icode[2], ~icode[1], ~icode[0]);  // AND_Gate
  and _0xa0 (_0xa0_out, icode[3], ~icode[2], icode[1], ~icode[0]);  // AND_Gate
  xor xor_1 (xor_1_out, _0x80_out, a_out);
  Multiplexer #(.width(32), .disabled(0)) multiplexer_1 (
    .in0(valP), .in1(valA), .out(out_4), .sel(a_out), .en(xor_1_out));

  // Notes on the sheet:
  //   p
endmodule

module toggle (
  input  in,
  input  Clk,
  input  reset,
  output out
);

  wire and_1_out, and_2_out, and_3_out, and_4_out, and_5_out, and_6_out;
  wire [1:0] or_2_out, register_1_q;

  and and_1 (and_1_out, ~register_1_q[1], register_1_q[0], ~in);  // AND_Gate
  and and_2 (and_2_out, ~register_1_q[1], ~register_1_q[0], in);  // AND_Gate
  and and_3 (and_3_out, register_1_q[1], ~register_1_q[0], ~in);  // AND_Gate
  and and_4 (and_4_out, ~register_1_q[1], register_1_q[0], in);  // AND_Gate
  Register #(.width(2)) register_1 (.D(or_2_out), .Q(register_1_q), .clk(Clk), .clr(reset));  // open: en
  and and_5 (and_5_out, register_1_q[1], ~register_1_q[0], in);  // AND_Gate
  and and_6 (and_6_out, register_1_q[1], register_1_q[0], in);
  or or_1 (or_2_out[1], and_1_out, and_3_out, and_5_out, and_6_out);
  or or_2 (or_2_out[0], and_2_out, and_4_out, and_5_out, and_6_out);
  or or_3 (out, and_1_out, and_4_out, and_3_out, and_5_out);
endmodule

// delay
module timing_helper (
  input  Clk,
  input  in,
  input  [7:0] delay,
  input  [7:0] length,
  input  [7:0] cycle,
  output [7:0] counter,
  output out
);

  wire comparator_1_eq, comparator_1_gt, comparator_2_gt, comparator_3_eq, d_ff_1_q, d_ff_2_q, not_1_out,
       or_1_out, or_2_out;
  wire [7:0] adder_1_out;

  Adder adder_1 (.a(delay), .b(length), .out(adder_1_out));  // open: cin, cout
  Counter counter_1 (.D(counter), .Q(counter), .clk(Clk), .clr(or_1_out));  // open: load, count, carry
  or or_1 (or_1_out, ~in, d_ff_1_q);  // OR_Gate
  Comparator #(.mode("unsigned")) comparator_1 (
    .a(counter), .b(delay), .gt(comparator_1_gt), .eq(comparator_1_eq));  // open: lt
  Comparator #(.mode("unsigned")) comparator_2 (.a(counter), .b(adder_1_out), .gt(comparator_2_gt));  // open: eq, lt
  Comparator #(.mode("unsigned")) comparator_3 (.a(counter), .b(cycle), .eq(comparator_3_eq));  // open: gt, lt
  or or_2 (or_2_out, comparator_1_gt, comparator_1_eq);
  D_Flip_Flop d_ff_1 (.clk(Clk), .D(comparator_3_eq), .Q(d_ff_1_q));  // open: Qn, preset, en, reset
  D_Flip_Flop d_ff_2 (.clk(Clk), .D(or_2_out), .Q(d_ff_2_q), .reset(comparator_2_gt));  // open: Qn, preset, en
  assign out = d_ff_2_q ? in : 1'bz;  // Controlled_Buffer controlled_buffer_1
  not not_1 (not_1_out, d_ff_2_q);
  assign out = not_1_out ? d_ff_2_q : 1'bz;  // Controlled_Buffer controlled_buffer_2
endmodule

// 2lE
module littleE (
  input  [31:0] bigE_in,
  output [31:0] littleE_out
);


  assign littleE_out = {bigE_in[7:0], bigE_in[15:8], bigE_in[23:16], bigE_in[31:24]};
endmodule

module bus_buffer (
  input  [7:0] i0,
  input  [7:0] i1,
  input  in_3,
  output [7:0] o0,
  output [7:0] o1
);

  wire not_1_out;

  assign o0 = not_1_out ? i0 : 8'bz;  // Controlled_Buffer controlled_buffer_1
  not not_1 (not_1_out, in_3);
  assign o1 = in_3 ? i1 : 8'bz;  // Controlled_Buffer controlled_buffer_2
endmodule

// pc
module PC (
  input  Clk,
  input  [31:0] in_2,
  output [31:0] out_3
);

  wire timing_helper_1_out;
  wire [7:0] timing_helper_1_counter;

  timing_helper timing_helper_1 (
    .delay(8'hf), .out(timing_helper_1_out), .in(1'b1), .length(8'h1), .cycle(8'hf), .Clk(Clk),
    .counter(timing_helper_1_counter));
  Register #(.width(32)) register_1 (.D(in_2), .en(timing_helper_1_out), .Q(out_3), .clk(Clk));  // open: clr
endmodule

// loop
module Loop (
  input  Clk,
  output [31:0] out_2
);

  wire comparator_1_eq, multiplexer_1_out;

  Counter #(.width(32), .max('hffffffff)) counter_1 (
    .count(Clk), .Q(out_2), .clk(Clk), .clr(multiplexer_1_out));  // open: load, D, carry
  Comparator #(.width(32)) comparator_1 (.a(out_2), .b(32'h6), .eq(comparator_1_eq));  // open: gt, lt
  Multiplexer #(.enable("false")) multiplexer_1 (
    .in0(1'b0), .in1(1'b1), .out(multiplexer_1_out), .sel(comparator_1_eq));
endmodule

// pc_incr
module PCIncr (
  input  [3:0] iCode,
  input  [31:0] curPC,
  output [31:0] valP
);

  wire [15:0] multiplexer_1_out;

  Multiplexer #(.select(4), .width(16), .enable("false")) multiplexer_1 (
    .in0({16{1'b0}}), .in1(16'h1), .in2(16'h2), .in3(16'h6), .in4(16'h6), .in5(16'h6), .in6(16'h2),
    .in7(16'h5), .in8(16'h5), .in9(16'h1), .in10(16'h2), .in11(16'h2), .out(multiplexer_1_out), .sel(iCode));  // open: in12, in13, in14, in15
  Adder #(.width(32)) adder_1 (.a({{16{1'b0}}, multiplexer_1_out}), .b(curPC), .out(valP));  // open: cin, cout
endmodule

// instr_mem
module FUnit (
  input  Clk,
  input  [31:0] new_pc,
  output [3:0] icode,
  output inst_err,
  output [3:0] ifun,
  output [3:0] rA,
  output [31:0] valC,
  output [3:0] rB,
  output [3:0] icode_2,
  output mem_err
);

  wire and_1_out, ful_1_clear, ful_1_data0, ful_1_data1, ful_1_data2, ful_1_data3, ful_1_icode_2, ful_1_ifun,
       not_2_out, not_3_out, register_6_q, timing_helper_1_out, val_instr_1_isvalid;
  wire [2:0] counter_1_q;
  wire [7:0] adder_1_out_2, rom_1_data, timing_helper_1_counter;
  wire [23:0] adder_1_out;

  timing_helper timing_helper_1 (
    .delay({8{1'b0}}), .out(timing_helper_1_out), .in(1'b1), .length(8'h6), .cycle(8'hf), .Clk(Clk),
    .counter(timing_helper_1_counter));
  not not_1 (inst_err, val_instr_1_isvalid);
  and and_1 (and_1_out, Clk, timing_helper_1_out);
  not not_2 (not_2_out, and_1_out);
  Counter #(.width(3), .max('h6)) counter_1 (
    .D(counter_1_q), .Q(counter_1_q), .clk(not_2_out));  // open: load, count, carry, clr
  val_instr val_instr_1 (.icode(icode), .ifun(ifun), .isValid(val_instr_1_isvalid));
  Comparator #(.mode("unsigned")) comparator_1 (.a({8{1'b0}}), .b(adder_1_out_2), .gt(mem_err));  // open: eq, lt
  not not_3 (not_3_out, and_1_out);
  Adder #(.width(32)) adder_1 (
    .a({{29{1'b0}}, counter_1_q}), .b(new_pc), .out({adder_1_out_2, adder_1_out}));  // open: cin, cout
  ROM #(.addrWidth(24)) rom_1 (.addr(adder_1_out), .data(rom_1_data), .sel(and_1_out));
  Register register_1 (.D(rom_1_data), .en(ful_1_icode_2), .Q({icode, ifun}), .clk(not_3_out));  // open: clr
  Register register_2 (.D(rom_1_data), .en(ful_1_ifun), .Q({rA, rB}), .clk(not_3_out), .clr(register_6_q));
  FUL ful_1 (
    .ICode(icode), .Count({1'b0, counter_1_q}), .iCode_2(ful_1_icode_2), .iFun(ful_1_ifun),
    .Data0(ful_1_data0), .Data1(ful_1_data1), .Data2(ful_1_data2), .Data3(ful_1_data3), .Clear(ful_1_clear));
  Register register_3 (.D(rom_1_data), .en(ful_1_data0), .Q(valC[7:0]), .clk(not_3_out), .clr(register_6_q));
  Register register_4 (.D(rom_1_data), .en(ful_1_data1), .Q(valC[15:8]), .clk(not_3_out), .clr(register_6_q));
  Register register_5 (.D(rom_1_data), .en(ful_1_data2), .Q(valC[23:16]), .clk(not_3_out), .clr(register_6_q));
  Register #(.width(1)) register_6 (.D(ful_1_clear), .Q(register_6_q), .clk(and_1_out));  // open: en, clr
  Register register_7 (.D(rom_1_data), .en(ful_1_data3), .Q(valC[31:24]), .clk(not_3_out), .clr(register_6_q));

  assign icode_2 = icode;

  // Notes on the sheet:
  //   contents of rom_1 (hex, n*v repeats v):
  //   30 f5 0 2 0 0 30 f4 0 2 0 0 30 f1 1 0 0 0 30 f2 1 0 0 0 61 21 30 f0 1 0 0 0 23 10 a0 f 30 f0 1 0 0 0
  //   21 10 a0 f 30 f0 1 0 0 0 24 10 a0 f 30 f0 1 0 0 0 22 10 a0 f 30 f0 1 0 0 0 25 10 a0 f 30 f0 1 0 0 0
  //   26 10 a0 f
endmodule

module FUL (
  input  [3:0] ICode,
  input  [3:0] Count,
  output iFun,
  output Data0,
  output Data1,
  output Data2,
  output Data3,
  output iCode_2,
  output Clear
);

  wire and_2_out, and_3_out, and_4_out, and_5_out, and_6_out, and_7_out, and_8_out, and_9_out,
       demultiplexer_1_out0, demultiplexer_1_out1, demultiplexer_1_out2, demultiplexer_1_out3,
       demultiplexer_1_out4, demultiplexer_1_out5, demultiplexer_1_out6, demultiplexer_1_out7,
       demultiplexer_1_out8, demultiplexer_1_out9, demultiplexer_1_out10, demultiplexer_1_out11,
       demultiplexer_2_out1, demultiplexer_2_out2, demultiplexer_2_out3, demultiplexer_2_out4,
       demultiplexer_2_out5, or_1_out, or_2_out, or_4_out, or_5_out, or_7_out, or_8_out, or_9_out, or_11_out,
       or_12_out, or_14_out;

  Demultiplexer #(.select(4), .enable("false")) demultiplexer_1 (
    .out0(demultiplexer_1_out0), .out1(demultiplexer_1_out1), .out2(demultiplexer_1_out2),
    .out3(demultiplexer_1_out3), .out4(demultiplexer_1_out4), .out5(demultiplexer_1_out5),
    .out6(demultiplexer_1_out6), .out7(demultiplexer_1_out7), .out8(demultiplexer_1_out8),
    .out9(demultiplexer_1_out9), .out10(demultiplexer_1_out10), .out11(demultiplexer_1_out11), .in(1'b1),
    .sel(ICode));  // open: out12, out13, out14, out15
  Demultiplexer #(.select(4), .enable("false")) demultiplexer_2 (
    .out0(Clear), .out1(demultiplexer_2_out1), .out2(demultiplexer_2_out2), .out3(demultiplexer_2_out3),
    .out4(demultiplexer_2_out4), .out5(demultiplexer_2_out5), .in(1'b1), .sel(Count));  // open: out6, out7, out8, out9, out10, out11, out12, out13, out14, out15
  and and_1 (iFun, or_1_out, demultiplexer_2_out1);
  or or_1 (or_1_out, or_2_out, demultiplexer_1_out10, demultiplexer_1_out11);
  or or_2 (or_2_out, demultiplexer_1_out2, demultiplexer_1_out3, demultiplexer_1_out4, demultiplexer_1_out5, demultiplexer_1_out6);
  or or_3 (Data0, and_2_out, and_3_out);
  and and_2 (and_2_out, or_4_out, demultiplexer_2_out1);
  or or_4 (or_4_out, demultiplexer_1_out7, demultiplexer_1_out8);
  and and_3 (and_3_out, demultiplexer_2_out2, or_5_out);
  or or_5 (or_5_out, demultiplexer_1_out3, demultiplexer_1_out4, demultiplexer_1_out5);
  or or_6 (Data1, and_4_out, and_5_out);
  and and_4 (and_4_out, or_7_out, demultiplexer_2_out2);
  or or_7 (or_7_out, demultiplexer_1_out7, demultiplexer_1_out8);
  and and_5 (and_5_out, demultiplexer_2_out3, or_8_out);
  or or_8 (or_8_out, demultiplexer_1_out3, demultiplexer_1_out4, demultiplexer_1_out5);
  or or_9 (or_9_out, demultiplexer_1_out7, demultiplexer_1_out8);
  or or_10 (Data2, and_7_out, and_6_out);
  and and_6 (and_6_out, demultiplexer_2_out4, or_11_out);
  and and_7 (and_7_out, or_9_out, demultiplexer_2_out3);
  or or_11 (or_11_out, demultiplexer_1_out3, demultiplexer_1_out4, demultiplexer_1_out5);
  and and_8 (and_8_out, or_12_out, demultiplexer_2_out4);
  or or_12 (or_12_out, demultiplexer_1_out7, demultiplexer_1_out8);
  or or_13 (Data3, and_8_out, and_9_out);
  and and_9 (and_9_out, demultiplexer_2_out5, or_14_out);
  or or_14 (or_14_out, demultiplexer_1_out3, demultiplexer_1_out4, demultiplexer_1_out5);

  assign iCode_2 = Clear;
endmodule

module register_file (
  input  [31:0] valE,
  input  [3:0] srcA,
  input  [3:0] destE,
  input  eSA,
  input  eDE,
  input  [3:0] srcB,
  input  [3:0] destM,
  input  eSB,
  input  eDM,
  input  [31:0] valM,
  input  in_11,
  output [31:0] out_12,
  output [31:0] out_13
);

  wire or_1_out, or_2_out, or_3_out, or_4_out, or_5_out, or_6_out, or_7_out, or_8_out, read_decoder_1_out_3,
       read_decoder_1_out_4, read_decoder_1_out_5, read_decoder_1_out_6, read_decoder_1_out_7,
       read_decoder_1_out_8, read_decoder_1_out_9, read_decoder_1_out_10, read_decoder_2_out_3,
       read_decoder_2_out_4, read_decoder_2_out_5, read_decoder_2_out_6, read_decoder_2_out_7,
       read_decoder_2_out_8, read_decoder_2_out_9, read_decoder_2_out_10;
  wire [1:0] write_decoder_2_out_3, write_decoder_2_out_4, write_decoder_2_out_5, write_decoder_2_out_6,
       write_decoder_2_out_7, write_decoder_2_out_8, write_decoder_2_out_9, write_decoder_2_out_10;
  wire [31:0] multiplexer_1_out, multiplexer_2_out, multiplexer_3_out, multiplexer_4_out, multiplexer_5_out,
       multiplexer_6_out, multiplexer_7_out, multiplexer_8_out, register_1_q, register_2_q, register_3_q,
       register_4_q, register_5_q, register_6_q, register_7_q, register_8_q;

  write_decoder write_decoder_1 (
    .w_addr(destE), .enable(eDE), .out_3(write_decoder_2_out_3[1]), .out_4(write_decoder_2_out_4[1]),
    .out_5(write_decoder_2_out_5[1]), .out_6(write_decoder_2_out_6[1]), .out_7(write_decoder_2_out_7[1]),
    .out_8(write_decoder_2_out_8[1]), .out_9(write_decoder_2_out_9[1]), .out_10(write_decoder_2_out_10[1]));
  write_decoder write_decoder_2 (
    .w_addr(destM), .enable(eDM), .out_3(write_decoder_2_out_3[0]), .out_4(write_decoder_2_out_4[0]),
    .out_5(write_decoder_2_out_5[0]), .out_6(write_decoder_2_out_6[0]), .out_7(write_decoder_2_out_7[0]),
    .out_8(write_decoder_2_out_8[0]), .out_9(write_decoder_2_out_9[0]), .out_10(write_decoder_2_out_10[0]));
  or or_1 (or_1_out, write_decoder_2_out_3[0], write_decoder_2_out_3[1]);
  or or_2 (or_2_out, write_decoder_2_out_4[0], write_decoder_2_out_4[1]);
  or or_3 (or_3_out, write_decoder_2_out_5[0], write_decoder_2_out_5[1]);
  or or_4 (or_4_out, write_decoder_2_out_6[0], write_decoder_2_out_6[1]);
  or or_5 (or_5_out, write_decoder_2_out_7[0], write_decoder_2_out_7[1]);
  or or_6 (or_6_out, write_decoder_2_out_8[0], write_decoder_2_out_8[1]);
  or or_7 (or_7_out, write_decoder_2_out_9[0], write_decoder_2_out_9[1]);
  or or_8 (or_8_out, write_decoder_2_out_10[0], write_decoder_2_out_10[1]);
  Multiplexer #(.select(2), .width(32)) multiplexer_1 (
    .in0(register_1_q), .in1(valM), .in2(valE), .in3(register_1_q), .out(multiplexer_1_out),
    .sel(write_decoder_2_out_3), .en(1'b1));
  Multiplexer #(.select(2), .width(32)) multiplexer_2 (
    .in0(register_2_q), .in1(valM), .in2(valE), .in3(register_2_q), .out(multiplexer_2_out),
    .sel(write_decoder_2_out_4), .en(1'b1));
  Multiplexer #(.select(2), .width(32)) multiplexer_3 (
    .in0(register_3_q), .in1(valM), .in2(valE), .in3(register_3_q), .out(multiplexer_3_out),
    .sel(write_decoder_2_out_5), .en(1'b1));
  Multiplexer #(.select(2), .width(32)) multiplexer_4 (
    .in0(register_4_q), .in1(valM), .in2(valE), .in3(register_4_q), .out(multiplexer_4_out),
    .sel(write_decoder_2_out_6), .en(1'b1));
  Multiplexer #(.select(2), .width(32)) multiplexer_5 (
    .in0(register_5_q), .in1(valM), .in2(valE), .in3(register_5_q), .out(multiplexer_5_out),
    .sel(write_decoder_2_out_7), .en(1'b1));
  Multiplexer #(.select(2), .width(32)) multiplexer_6 (
    .in0(register_6_q), .in1(valM), .in2(valE), .in3(register_6_q), .out(multiplexer_6_out),
    .sel(write_decoder_2_out_8), .en(1'b1));
  Multiplexer #(.select(2), .width(32)) multiplexer_7 (
    .in0(register_7_q), .in1(valM), .in2(valE), .in3(register_7_q), .out(multiplexer_7_out),
    .sel(write_decoder_2_out_9), .en(1'b1));
  Multiplexer #(.select(2), .width(32)) multiplexer_8 (
    .in0(register_8_q), .in1(valM), .in2(valE), .in3(register_8_q), .out(multiplexer_8_out),
    .sel(write_decoder_2_out_10), .en(1'b1));
  Register #(.width(32)) register_1 (.D(multiplexer_1_out), .en(or_1_out), .Q(register_1_q), .clk(in_11));  // open: clr
  Register #(.width(32)) register_2 (.D(multiplexer_2_out), .en(or_2_out), .Q(register_2_q), .clk(in_11));  // open: clr
  Register #(.width(32)) register_3 (.D(multiplexer_3_out), .en(or_3_out), .Q(register_3_q), .clk(in_11));  // open: clr
  Register #(.width(32)) register_4 (.D(multiplexer_4_out), .en(or_4_out), .Q(register_4_q), .clk(in_11));  // open: clr
  Register #(.width(32)) register_5 (.D(multiplexer_5_out), .en(or_5_out), .Q(register_5_q), .clk(in_11));  // open: clr
  Register #(.width(32)) register_6 (.D(multiplexer_6_out), .en(or_6_out), .Q(register_6_q), .clk(in_11));  // open: clr
  Register #(.width(32)) register_7 (.D(multiplexer_7_out), .en(or_7_out), .Q(register_7_q), .clk(in_11));  // open: clr
  Register #(.width(32)) register_8 (.D(multiplexer_8_out), .en(or_8_out), .Q(register_8_q), .clk(in_11));  // open: clr
  assign out_12 = read_decoder_1_out_3 ? register_1_q : 32'bz;  // Controlled_Buffer controlled_buffer_1
  assign out_12 = read_decoder_1_out_4 ? register_2_q : 32'bz;  // Controlled_Buffer controlled_buffer_2
  assign out_12 = read_decoder_1_out_5 ? register_3_q : 32'bz;  // Controlled_Buffer controlled_buffer_3
  assign out_12 = read_decoder_1_out_6 ? register_4_q : 32'bz;  // Controlled_Buffer controlled_buffer_4
  assign out_12 = read_decoder_1_out_7 ? register_5_q : 32'bz;  // Controlled_Buffer controlled_buffer_5
  assign out_12 = read_decoder_1_out_8 ? register_6_q : 32'bz;  // Controlled_Buffer controlled_buffer_6
  assign out_12 = read_decoder_1_out_9 ? register_7_q : 32'bz;  // Controlled_Buffer controlled_buffer_7
  assign out_12 = read_decoder_1_out_10 ? register_8_q : 32'bz;  // Controlled_Buffer controlled_buffer_8
  assign out_13 = read_decoder_2_out_3 ? register_1_q : 32'bz;  // Controlled_Buffer controlled_buffer_9
  assign out_13 = read_decoder_2_out_4 ? register_2_q : 32'bz;  // Controlled_Buffer controlled_buffer_10
  assign out_13 = read_decoder_2_out_5 ? register_3_q : 32'bz;  // Controlled_Buffer controlled_buffer_11
  assign out_13 = read_decoder_2_out_6 ? register_4_q : 32'bz;  // Controlled_Buffer controlled_buffer_12
  assign out_13 = read_decoder_2_out_7 ? register_5_q : 32'bz;  // Controlled_Buffer controlled_buffer_13
  assign out_13 = read_decoder_2_out_8 ? register_6_q : 32'bz;  // Controlled_Buffer controlled_buffer_14
  assign out_13 = read_decoder_2_out_9 ? register_7_q : 32'bz;  // Controlled_Buffer controlled_buffer_15
  assign out_13 = read_decoder_2_out_10 ? register_8_q : 32'bz;  // Controlled_Buffer controlled_buffer_16
  read_decoder read_decoder_1 (
    .w_addr(srcA), .enable(eSA), .out_3(read_decoder_1_out_3), .out_4(read_decoder_1_out_4),
    .out_5(read_decoder_1_out_5), .out_6(read_decoder_1_out_6), .out_7(read_decoder_1_out_7),
    .out_8(read_decoder_1_out_8), .out_9(read_decoder_1_out_9), .out_10(read_decoder_1_out_10));
  read_decoder read_decoder_2 (
    .w_addr(srcB), .enable(eSB), .out_3(read_decoder_2_out_3), .out_4(read_decoder_2_out_4),
    .out_5(read_decoder_2_out_5), .out_6(read_decoder_2_out_6), .out_7(read_decoder_2_out_7),
    .out_8(read_decoder_2_out_8), .out_9(read_decoder_2_out_9), .out_10(read_decoder_2_out_10));
endmodule

module write_decoder (
  input  [3:0] w_addr,
  input  enable,
  output out_3,
  output out_4,
  output out_5,
  output out_6,
  output out_7,
  output out_8,
  output out_9,
  output out_10
);

  Demultiplexer #(.select(4)) demultiplexer_1 (
    .out0(out_3), .out1(out_4), .out2(out_5), .out3(out_6), .out4(out_7), .out5(out_8), .out6(out_9),
    .out7(out_10), .in(1'b1), .sel(w_addr), .en(enable));  // open: out8, out9, out10, out11, out12, out13, out14, out15
endmodule

module read_decoder (
  input  [3:0] w_addr,
  input  enable,
  output out_3,
  output out_4,
  output out_5,
  output out_6,
  output out_7,
  output out_8,
  output out_9,
  output out_10
);

  Demultiplexer #(.select(4)) demultiplexer_1 (
    .out0(out_3), .out1(out_4), .out2(out_5), .out3(out_6), .out4(out_7), .out5(out_8), .out6(out_9),
    .out7(out_10), .in(1'b1), .sel(w_addr), .en(enable));  // open: out8, out9, out10, out11, out12, out13, out14, out15
endmodule

module srcA (
  input  [3:0] icode,
  input  [3:0] rA,
  output [3:0] out_3
);

  Multiplexer #(.select(4), .width(4)) multiplexer_1 (
    .in0(4'b1111), .in1(4'b1111), .in2(rA), .in3(4'b1111), .in4(rA), .in5(rA), .in6(rA), .in7(4'b1111),
    .in8(4'b1111), .in9(4'b0100), .in10(rA), .in11(4'b0100), .out(out_3), .sel(icode), .en(1'b1));  // open: in12, in13, in14, in15
endmodule

module srcB (
  input  [3:0] icode,
  input  [3:0] rB,
  output [3:0] out_3
);

  Multiplexer #(.select(4), .width(4)) multiplexer_1 (
    .in0(4'b1111), .in1(4'b1111), .in2(rB), .in3(rB), .in4(rB), .in5(rB), .in6(rB), .in7(4'b1111),
    .in8(4'b0100), .in9(4'b0100), .in10(4'b0100), .in11(4'b0100), .out(out_3), .sel(icode), .en(1'b1));  // open: in12, in13, in14, in15
endmodule

module dstE (
  input  [3:0] icode,
  input  [3:0] rB,
  input  [3:0] ifun,
  input  [2:0] Cnd,
  output [3:0] out_5
);

  wire cnd_decode_1_out, not_1_out;
  wire [3:0] controlled_buffer_1_out;

  cnd_decode cnd_decode_1 (.ifun(ifun), .Cnd(Cnd), .out(cnd_decode_1_out));
  Multiplexer #(.select(4), .width(4)) multiplexer_1 (
    .in0(4'b1111), .in1(4'b1111), .in2(controlled_buffer_1_out), .in3(rB), .in4(4'b1111), .in5(4'b1111),
    .in6(rB), .in7(4'b1111), .in8(4'b0100), .in9(4'b0100), .in10(4'b0100), .in11(4'b0100), .out(out_5),
    .sel(icode), .en(1'b1));  // open: in12, in13, in14, in15
  not not_1 (not_1_out, cnd_decode_1_out);
  assign controlled_buffer_1_out = not_1_out ? 4'b1111 : 4'bz;  // Controlled_Buffer controlled_buffer_1
  assign controlled_buffer_1_out = cnd_decode_1_out ? rB : 4'bz;  // Controlled_Buffer controlled_buffer_2
endmodule

module dstM (
  input  [3:0] icode,
  input  [3:0] rA,
  output [3:0] out_3
);

  Multiplexer #(.select(4), .width(4)) multiplexer_1 (
    .in0(4'b1111), .in1(4'b1111), .in2(4'b1111), .in3(4'b1111), .in4(4'b1111), .in5(rA), .in6(4'b1111),
    .in7(4'b1111), .in8(4'b1111), .in9(4'b1111), .in10(4'b1111), .in11(rA), .out(out_3), .sel(icode),
    .en(1'b1));  // open: in12, in13, in14, in15
endmodule

module stat (
  input  instr_err,
  input  [3:0] icode,
  input  mem_err,
  output [1:0] out_4
);

  wire [1:1] and_1_out;

  and and_1 (and_1_out[1], ~icode[3], ~icode[2], ~icode[1], ~icode[0]);  // AND_Gate
  Multiplexer #(.select(3), .width(2)) multiplexer_1 (
    .in0(2'b00), .in1(2'b10), .in2(2'b01), .in3(2'b11), .in4(2'b11), .in5(2'b11), .in6(2'b11), .in7(2'b11),
    .out(out_4), .sel({mem_err, and_1_out[1], instr_err}));  // open: en
endmodule

module cnd_decode (
  input  [3:0] ifun,
  input  [2:0] Cnd,
  output out
);

  wire and_1_out, not_1_out, not_2_out, or_1_out, xor_1_out;

  not not_1 (not_1_out, Cnd[0]);
  not not_2 (not_2_out, xor_1_out);
  xor xor_1 (xor_1_out, Cnd[2], Cnd[1]);
  or or_1 (or_1_out, Cnd[0], xor_1_out);
  and and_1 (and_1_out, not_2_out, not_1_out);
  Multiplexer #(.select(4)) multiplexer_1 (
    .in0(1'b1), .in1(or_1_out), .in2(xor_1_out), .in3(Cnd[0]), .in4(not_1_out), .in5(not_2_out),
    .in6(and_1_out), .out(out), .sel(ifun));  // open: in7, in8, in9, in10, in11, in12, in13, in14, in15, en
endmodule

module new_pc (
  input  [3:0] icode,
  input  [3:0] ifun,
  input  [2:0] Cnd,
  input  [31:0] valC,
  input  [31:0] valM,
  input  [31:0] valP,
  output [31:0] out
);

  wire cnd_decode_1_out, not_1_out;
  wire [31:0] controlled_buffer_1_out;

  cnd_decode cnd_decode_1 (.ifun(ifun), .Cnd(Cnd), .out(cnd_decode_1_out));
  assign controlled_buffer_1_out = cnd_decode_1_out ? valC : 32'bz;  // Controlled_Buffer controlled_buffer_1
  assign controlled_buffer_1_out = not_1_out ? valP : 32'bz;  // Controlled_Buffer controlled_buffer_2
  not not_1 (not_1_out, cnd_decode_1_out);
  Multiplexer #(.select(4), .width(32)) multiplexer_1 (
    .in0(valP), .in1(valP), .in2(valP), .in3(valP), .in4(valP), .in5(valP), .in6(valP),
    .in7(controlled_buffer_1_out), .in8(valC), .in9(valM), .in10(valP), .in11(valP), .out(out), .sel(icode));  // open: in12, in13, in14, in15, en
endmodule

// valInstr
module val_instr (
  input  [3:0] icode,
  input  [3:0] ifun,
  output isValid
);

  wire and_1_out, and_2_out, and_3_out, and_4_out, comparator_1_eq, comparator_2_lt, comparator_3_lt,
       multiplexer_1_out, multiplexer_2_out;

  Comparator #(.width(4), .mode("unsigned")) comparator_1 (
    .a(ifun), .b(4'b0000), .eq(comparator_1_eq));  // open: gt, lt
  Comparator #(.width(4), .mode("unsigned")) comparator_2 (
    .a(ifun), .b(4'b0111), .lt(comparator_2_lt));  // open: gt, eq
  Comparator #(.width(4), .mode("unsigned")) comparator_3 (
    .a(ifun), .b(4'b0100), .lt(comparator_3_lt));  // open: gt, eq
  and and_1 (and_1_out, ~icode[0], icode[1], icode[2], ~icode[3]);  // AND_Gate
  Multiplexer #(.select(4)) multiplexer_1 (
    .in0(1'b1), .in1(1'b1), .in2(1'b0), .in3(1'b1), .in4(1'b1), .in5(1'b1), .in6(1'b0), .in7(1'b0),
    .in8(1'b1), .in9(1'b1), .in10(1'b1), .in11(1'b1), .in12(1'b0), .in13(1'b0), .in14(1'b0), .in15(1'b0),
    .out(multiplexer_1_out), .sel(icode));  // open: en
  Multiplexer #(.select(4)) multiplexer_2 (
    .in0(1'b0), .in1(1'b0), .in2(1'b1), .in3(1'b0), .in4(1'b0), .in5(1'b0), .in6(1'b0), .in7(1'b1),
    .in8(1'b0), .in9(1'b0), .in10(1'b0), .in11(1'b0), .in12(1'b0), .in13(1'b0), .in14(1'b0), .in15(1'b0),
    .out(multiplexer_2_out), .sel(icode));  // open: en
  and and_2 (and_2_out, multiplexer_1_out, comparator_1_eq);
  and and_3 (and_3_out, multiplexer_2_out, comparator_2_lt);
  and and_4 (and_4_out, and_1_out, comparator_3_lt);
  or or_1 (isValid, and_2_out, and_3_out, and_4_out);
endmodule

// A
module ALUA (
  input  [1:0] ALUA_Function,
  input  [31:0] ValC,
  input  [31:0] ValA,
  output [31:0] ALUAOUT
);

  wire comparator_1_eq, comparator_1_gt, comparator_2_eq, comparator_3_eq, or_1_out;
  wire [31:0] adder_1_out;

  assign ALUAOUT = comparator_2_eq ? ValC : 32'bz;  // Controlled_Buffer controlled_buffer_1
  assign ALUAOUT = or_1_out ? ValA : 32'bz;  // Controlled_Buffer controlled_buffer_2
  assign ALUAOUT = comparator_3_eq ? adder_1_out : 32'bz;  // Controlled_Buffer controlled_buffer_3
  Adder #(.width(32)) adder_1 (.a(ValC), .b(ValA), .out(adder_1_out));  // open: cin, cout
  Comparator #(.width(2)) comparator_1 (
    .a(ALUA_Function), .b(2'b01), .gt(comparator_1_gt), .eq(comparator_1_eq));  // open: lt
  Comparator #(.width(2)) comparator_2 (.a(ALUA_Function), .b(2'b10), .eq(comparator_2_eq));  // open: gt, lt
  Comparator #(.width(2)) comparator_3 (.a(ALUA_Function), .b(2'b11), .eq(comparator_3_eq));  // open: gt, lt
  or or_1 (or_1_out, comparator_1_gt, comparator_1_eq);
endmodule

// B
module ALUB (
  input  [31:0] ValB,
  output [31:0] ALUBOUT
);


  assign ALUBOUT = ValB;
endmodule

// afun
module ALUFun (
  input  [3:0] iCode,
  input  [3:0] iFun,
  output Valid,
  output [1:0] ALUA,
  output [3:0] ALUE
);

  wire demultiplexer_1_out0, demultiplexer_1_out1, demultiplexer_1_out2, demultiplexer_1_out3,
       demultiplexer_1_out4, demultiplexer_1_out5, demultiplexer_1_out6, demultiplexer_1_out7,
       demultiplexer_1_out8, demultiplexer_1_out9, demultiplexer_1_out10, demultiplexer_1_out11;

  Multiplexer #(.select(4), .enable("false")) multiplexer_1 (
    .in0(1'b0), .in1(1'b0), .in2(1'b0), .in3(1'b0), .in4(1'b0), .in5(1'b0), .in6(1'b1), .in7(1'b0),
    .in8(1'b0), .in9(1'b0), .in10(1'b0), .in11(1'b0), .in12(1'b0), .in13(1'b0), .in14(1'b0), .in15(1'b0),
    .out(Valid), .sel(iCode));
  Demultiplexer #(.select(4), .enable("false")) demultiplexer_1 (
    .out0(demultiplexer_1_out0), .out1(demultiplexer_1_out1), .out2(demultiplexer_1_out2),
    .out3(demultiplexer_1_out3), .out4(demultiplexer_1_out4), .out5(demultiplexer_1_out5),
    .out6(demultiplexer_1_out6), .out7(demultiplexer_1_out7), .out8(demultiplexer_1_out8),
    .out9(demultiplexer_1_out9), .out10(demultiplexer_1_out10), .out11(demultiplexer_1_out11), .in(1'b1),
    .sel(iCode));  // open: out12, out13, out14, out15
  Instr0 instr0_1 (.iFun(iFun), .Enable(demultiplexer_1_out0), .out_3(ALUA), .out_5(ALUE));  // open: out_4
  Instr1 instr1_1 (.iFun(iFun), .Enable(demultiplexer_1_out1), .out_3(ALUA), .out_5(ALUE));  // open: out_4
  Instr2 instr2_1 (.iFun(iFun), .Enable(demultiplexer_1_out2), .out_3(ALUA), .out_5(ALUE));  // open: out_4
  Instr3 instr3_1 (.iFun(iFun), .Enable(demultiplexer_1_out3), .out_3(ALUA), .out_5(ALUE));  // open: out_4
  Instr4 instr4_1 (.iFun(iFun), .Enable(demultiplexer_1_out4), .out_3(ALUA), .out_5(ALUE));  // open: out_4
  Instr5 instr5_1 (.iFun(iFun), .Enable(demultiplexer_1_out5), .out_3(ALUA), .out_5(ALUE));  // open: out_4
  Instr6 instr6_1 (.iFun(iFun), .Enable(demultiplexer_1_out6), .out_3(ALUA), .out_5(ALUE));  // open: out_4
  Instr7 instr7_1 (.iFun(iFun), .Enable(demultiplexer_1_out7), .out_3(ALUA), .out_5(ALUE));  // open: out_4
  Instr8 instr8_1 (.iFun(iFun), .Enable(demultiplexer_1_out8), .out_3(ALUA), .out_5(ALUE));  // open: out_4
  Instr9 instr9_1 (.iFun(iFun), .Enable(demultiplexer_1_out9), .out_3(ALUA), .out_5(ALUE));  // open: out_4
  InstrA instra_1 (.iFun(iFun), .Enable(demultiplexer_1_out10), .out_3(ALUA), .out_5(ALUE));  // open: out_4
  InstrB instrb_1 (.iFun(iFun), .Enable(demultiplexer_1_out11), .out_3(ALUA), .out_5(ALUE));  // open: out_4
endmodule

module Instr0 (
  input  [3:0] iFun,
  input  Enable,
  output [1:0] out_3,
  output out_4,
  output [3:0] out_5
);

  assign out_3 = Enable ? 2'b00 : 2'bz;  // Controlled_Buffer controlled_buffer_1
  assign out_5 = Enable ? 4'b0000 : 4'bz;  // Controlled_Buffer controlled_buffer_2
  assign out_4 = Enable ? 1'b0 : 1'bz;  // Controlled_Buffer controlled_buffer_3
endmodule

module Instr1 (
  input  [3:0] iFun,
  input  Enable,
  output [1:0] out_3,
  output out_4,
  output [3:0] out_5
);

  assign out_3 = Enable ? 2'b00 : 2'bz;  // Controlled_Buffer controlled_buffer_1
  assign out_5 = Enable ? 4'b0000 : 4'bz;  // Controlled_Buffer controlled_buffer_2
  assign out_4 = Enable ? 1'b0 : 1'bz;  // Controlled_Buffer controlled_buffer_3
endmodule

module Instr2 (
  input  [3:0] iFun,
  input  Enable,
  output [1:0] out_3,
  output out_4,
  output [3:0] out_5
);

  assign out_3 = Enable ? 2'b01 : 2'bz;  // Controlled_Buffer controlled_buffer_1
  assign out_5 = Enable ? 4'b0000 : 4'bz;  // Controlled_Buffer controlled_buffer_2
  assign out_4 = Enable ? 1'b0 : 1'bz;  // Controlled_Buffer controlled_buffer_3
endmodule

module Instr3 (
  input  [3:0] iFun,
  input  Enable,
  output [1:0] out_3,
  output out_4,
  output [3:0] out_5
);

  assign out_3 = Enable ? 2'b10 : 2'bz;  // Controlled_Buffer controlled_buffer_1
  assign out_5 = Enable ? 4'b0000 : 4'bz;  // Controlled_Buffer controlled_buffer_2
  assign out_4 = Enable ? 1'b0 : 1'bz;  // Controlled_Buffer controlled_buffer_3
endmodule

module Instr4 (
  input  [3:0] iFun,
  input  Enable,
  output [1:0] out_3,
  output out_4,
  output [3:0] out_5
);

  assign out_3 = Enable ? 2'b10 : 2'bz;  // Controlled_Buffer controlled_buffer_1
  assign out_5 = Enable ? 4'b0001 : 4'bz;  // Controlled_Buffer controlled_buffer_2
  assign out_4 = Enable ? 1'b1 : 1'bz;  // Controlled_Buffer controlled_buffer_3
endmodule

module Instr5 (
  input  [3:0] iFun,
  input  Enable,
  output [1:0] out_3,
  output out_4,
  output [3:0] out_5
);

  assign out_3 = Enable ? 2'b10 : 2'bz;  // Controlled_Buffer controlled_buffer_1
  assign out_5 = Enable ? 4'b0001 : 4'bz;  // Controlled_Buffer controlled_buffer_2
  assign out_4 = Enable ? 1'b0 : 1'bz;  // Controlled_Buffer controlled_buffer_3
endmodule

module Instr6 (
  input  [3:0] iFun,
  input  Enable,
  output [1:0] out_3,
  output out_4,
  output [3:0] out_5
);

  wire [3:0] adder_1_out;

  assign out_3 = Enable ? 2'b01 : 2'bz;  // Controlled_Buffer controlled_buffer_1
  Adder #(.width(4)) adder_1 (.a(4'b0001), .b(iFun), .out(adder_1_out));  // open: cin, cout
  assign out_5 = Enable ? adder_1_out : 4'bz;  // Controlled_Buffer controlled_buffer_2
  assign out_4 = Enable ? 1'b1 : 1'bz;  // Controlled_Buffer controlled_buffer_3
endmodule

module Instr7 (
  input  [3:0] iFun,
  input  Enable,
  output [1:0] out_3,
  output out_4,
  output [3:0] out_5
);

  assign out_3 = Enable ? 2'b00 : 2'bz;  // Controlled_Buffer controlled_buffer_1
  assign out_5 = Enable ? 4'b0000 : 4'bz;  // Controlled_Buffer controlled_buffer_2
  assign out_4 = Enable ? 1'b0 : 1'bz;  // Controlled_Buffer controlled_buffer_3
endmodule

module Instr8 (
  input  [3:0] iFun,
  input  Enable,
  output [1:0] out_3,
  output out_4,
  output [3:0] out_5
);

  assign out_3 = Enable ? 2'b00 : 2'bz;  // Controlled_Buffer controlled_buffer_1
  assign out_5 = Enable ? 4'b0010 : 4'bz;  // Controlled_Buffer controlled_buffer_2
  assign out_4 = Enable ? 1'b1 : 1'bz;  // Controlled_Buffer controlled_buffer_3
endmodule

module Instr9 (
  input  [3:0] iFun,
  input  Enable,
  output [1:0] out_3,
  output out_4,
  output [3:0] out_5
);

  assign out_3 = Enable ? 2'b00 : 2'bz;  // Controlled_Buffer controlled_buffer_1
  assign out_5 = Enable ? 4'b0001 : 4'bz;  // Controlled_Buffer controlled_buffer_2
  assign out_4 = Enable ? 1'b1 : 1'bz;  // Controlled_Buffer controlled_buffer_3
endmodule

module InstrA (
  input  [3:0] iFun,
  input  Enable,
  output [1:0] out_3,
  output out_4,
  output [3:0] out_5
);

  assign out_3 = Enable ? 2'b00 : 2'bz;  // Controlled_Buffer controlled_buffer_1
  assign out_5 = Enable ? 4'b0010 : 4'bz;  // Controlled_Buffer controlled_buffer_2
  assign out_4 = Enable ? 1'b1 : 1'bz;  // Controlled_Buffer controlled_buffer_3
endmodule

module InstrB (
  input  [3:0] iFun,
  input  Enable,
  output [1:0] out_3,
  output out_4,
  output [3:0] out_5
);

  assign out_3 = Enable ? 2'b00 : 2'bz;  // Controlled_Buffer controlled_buffer_1
  assign out_5 = Enable ? 4'b0001 : 4'bz;  // Controlled_Buffer controlled_buffer_2
  assign out_4 = Enable ? 1'b1 : 1'bz;  // Controlled_Buffer controlled_buffer_3
endmodule

module ALU (
  input  [3:0] Function,
  input  [31:0] valA,
  input  [31:0] valB,
  input  [3:0] in_4,
  output ZF,
  output [31:0] ValE,
  output A,
  output B,
  output C
);

  wire comparator_2_eq, comparator_3_eq, comparator_4_eq, comparator_5_eq, not_1_out, Stack_Movement_out;
  wire [30:0] controlled_buffer_1_out;
  wire [31:0] adder_1_out, Andl_out, subtractor_1_out, Xorl_out;

  Comparator #(.width(32)) comparator_1 (.a({C, ValE[30:0]}), .b({32{1'b0}}), .eq(ZF));  // open: gt, lt
  assign {A, controlled_buffer_1_out} = Stack_Movement_out ? 32'h4 : 32'bz;  // Controlled_Buffer controlled_buffer_1
  assign {A, controlled_buffer_1_out} = not_1_out ? valA : 32'bz;  // Controlled_Buffer controlled_buffer_2
  not not_1 (not_1_out, Stack_Movement_out);
  Comparator #(.width(4)) comparator_2 (.a(in_4), .b(4'b1000), .eq(comparator_2_eq));  // open: gt, lt
  Comparator #(.width(4)) comparator_3 (.a(in_4), .b(4'b1001), .eq(comparator_3_eq));  // open: gt, lt
  Comparator #(.width(4)) comparator_4 (.a(in_4), .b(4'b1010), .eq(comparator_4_eq));  // open: gt, lt
  Comparator #(.width(4)) comparator_5 (.a(in_4), .b(4'b1011), .eq(comparator_5_eq));  // open: gt, lt
  or Stack_Movement (Stack_Movement_out, comparator_2_eq, comparator_3_eq, comparator_4_eq, comparator_5_eq);
  Adder #(.width(32)) adder_1 (.a({A, controlled_buffer_1_out}), .b(valB), .out(adder_1_out));  // open: cin, cout
  Subtractor #(.width(32)) subtractor_1 (
    .a(valB), .b({A, controlled_buffer_1_out}), .out(subtractor_1_out));  // open: bin, bout
  Multiplexer #(.select(4), .width(32), .enable("false")) multiplexer_1 (
    .in0(valA), .in1(adder_1_out), .in2(subtractor_1_out), .in3(Andl_out), .in4(Xorl_out), .in5(valA),
    .out({C, ValE[30:0]}), .sel(Function));  // open: in6, in7, in8, in9, in10, in11, in12, in13, in14, in15
  assign Andl_out = {A, controlled_buffer_1_out} & valB;  // AND_Gate Andl, 32 bits wide
  assign Xorl_out = {A, controlled_buffer_1_out} ^ valB;  // XOR_Gate Xorl, 32 bits wide

  assign B = valB[31];
  assign ValE[31] = C;
endmodule

module Cnd (
  input  [3:0] Current_ALU_Function,
  input  Clk,
  input  Z,
  input  A,
  input  B,
  input  C,
  input  [3:0] icode,
  output [2:0] Cnd
);

  wire _2_2_out, _2_out, and_1_out, and_2_out, comparator_1_eq, comparator_2_eq, not_1_out, not_2_out,
       not_3_out, timing_helper_1_out;
  wire [2:2] OF_out;

  and and_1 (and_1_out, ~icode[0], icode[1], icode[2], ~icode[3]);  // AND_Gate
  timing_helper timing_helper_1 (
    .delay(8'h6), .out(timing_helper_1_out), .in(1'b1), .length(8'h2), .cycle(8'hf), .Clk(Clk));  // open: counter
  and and_2 (and_2_out, timing_helper_1_out, and_1_out);
  Register #(.width(3)) register_1 (.D({OF_out[2], C, Z}), .en(and_2_out), .Q(Cnd), .clk(Clk));  // open: clr
  and _2 (_2_out, A, comparator_2_eq, B, not_3_out);
  not not_1 (not_1_out, B);
  not not_2 (not_2_out, A);
  not not_3 (not_3_out, C);
  and _2_2 (_2_2_out, not_2_out, not_1_out, comparator_1_eq, C);
  or OF (OF_out[2], _2_out, _2_2_out);
  Comparator #(.width(4), .mode("unsigned")) comparator_1 (
    .a(Current_ALU_Function), .b(4'b0001), .eq(comparator_1_eq));  // open: gt, lt
  Comparator #(.width(4), .mode("unsigned")) comparator_2 (
    .a(Current_ALU_Function), .b(4'b0010), .eq(comparator_2_eq));  // open: gt, lt
endmodule
